# Fritzing sketch arduino_blink_pir_motion (saved by Fritzing 0.8.7b)
circuit board: 7.23835cm x 5.60482cm
breadboards: 1

parts:
  R1 = Resistor [tolerance=±5% resistance=10k package=THT]
  LED1 = LED - 5mm [color="Yellow (585nm)" package="5 mm [THT]"]
  R2 = Resistor [tolerance=±5% resistance=330 package=THT]
  PIR4 = PIR sensor 8630
  Part1 = Arduino Uno (Rev3) - ICSP

nets:
  N1: R1.Pin_0, Part1.5V
  N2: R1.Pin_1, PIR4.SIG, Part1.D2
  GND: LED1.cathode, PIR4.GND, Part1.GND
  N3: LED1.anode, R2.Pin_0
  N4: R2.Pin_1, Part1.ICSP_SCK, Part1.D13/SCK
  VDD: PIR4.VDD, Part1.VIN

custom parts:
  PIR sensor 8630: PIR sensor SEN-08630
